# Fritzing sketch Tray_Iter_1 (saved by Fritzing 0.9.3b)
breadboards: 1

parts:
  S1 = Pushbutton [package="[THT]"]
  S2 = Pushbutton [package="[THT]"]
  S3 = Pushbutton [package="[THT]"]
  R1 = Resistor [tolerance=±5% resistance=1k package=THT]
  R2 = Resistor [tolerance=±5% resistance=1k package=THT]
  R3 = Resistor [tolerance=±5% resistance=1k package=THT]
  R4 = Resistor [tolerance=±5% resistance=1k package=THT]
  R5 = Resistor [tolerance=±5% resistance=2k package=THT]
  S4 = Pushbutton [package="[THT]"]
  Part1 = Arduino Uno (Rev3)

nets:
  N1: S1.Pin_1, S1.Pin_2, S2.Pin_1, S2.Pin_2, S3.Pin_1, S3.Pin_2, S4.Pin_1, S4.Pin_2, Part1.GND
  N2: S1.Pin_3, S1.Pin_4, R1.Pin_0
  N3: S2.Pin_3, S2.Pin_4, R1.Pin_1, R2.Pin_0
  N4: S3.Pin_3, S3.Pin_4, R2.Pin_1, R3.Pin_0
  N5: R3.Pin_1, R4.Pin_0, S4.Pin_3, S4.Pin_4
  N6: R4.Pin_1, R5.Pin_0, Part1.A0
  N7: R5.Pin_1, Part1.3V3
